# Fritzing sketch init (saved by Fritzing 0.9.3b)
breadboards: 1

parts:
  부품1 = Arduino Nano (Rev3.0)
  ZS-042_RTC1 = ZS-042 RTC Module
  U1 = Molex Picoblade Series Header [part_number=0533980271 package=Picoblade-53398-0271]
  Grove1 = Grove OLED 128x96
  Power_RGB1 = Prolight RGB 3 Watt Star
  부품2 = YC164 [package=YC164]
  U2 = Molex Picoblade Series Header [part_number=0533980271 package=Picoblade-53398-0271]
  JP1 = Header 2 [package=molex-1x2_lock]
  JP2 = Header 2 [package=molex-1x2_lock]
  S1 = Pushbutton [package="[SMD]"]
  U3 = Molex Picoblade Series Header [part_number=0533980271 package=Picoblade-53398-0271]

nets:
  N1: 부품1.D3, 부품2.5
  N2: 부품1.D7, S1.Pin_3, S1.Pin_4
  N3: 부품1.VIN, JP1.1, U3.1
  GND: 부품1.GND, ZS-042_RTC1.GND, Grove1.GND, JP1.2, S1.Pin_1, S1.Pin_2, U3.2
  VCC: 부품1.5V, ZS-042_RTC1.VCC, ZS-042_RTC1.SDA, Grove1.VCC
  N4: 부품1.A5, ZS-042_RTC1.SCL, Grove1.SCL
  N5: 부품1.A4, Grove1.SDA
  N6: U1.1, 부품2.7
  N7: U1.2, 부품2.6
  N8: Power_RGB1.B+, JP2.2
  N9: Power_RGB1.B-, JP2.1
  N10: 부품2.2, U2.2
  N11: 부품2.3, U2.1
