# Fritzing sketch light (saved by Fritzing 0.9.3b)
circuit board: 4cm x 9cm
breadboards: 1

parts:
  Temp = Header 3 [part_number="Temp. Sensor" package=molex-1x3_lock]
  부품2 = Arduino Nano (Rev3.0) (ICSP)
  Q2 = Basic FET N-Channel [package="DPak [SMD]"]
  Fan = Header 2 [part_number=Fan package=molex-1x2_lock]
  R3 = Resistor [tolerance=±5% resistance=100 package="2512 [SMD]"]
  R4 = Resistor [tolerance=±5% resistance=10k package="2512 [SMD]"]
  X1 = USB Connectors [package=usb-minib]
  C1 = Capacitor [package=cap-pth-small2]
  PWM = Header 4 [package=molex-1x4_lock]

nets:
  N1: Temp.1, 부품2.D7
  GND: Temp.2, 부품2.GND, Q2.source, R4.Pin_1, X1.GND
  N2: Temp.3, 부품2.VIN, Fan.2, X1.VBUS, C1.2
  N3: 부품2.D3, R3.Pin_0
  N4: 부품2.D5, PWM.4
  N5: 부품2.D6, PWM.3
  N6: 부품2.D9, PWM.2
  N7: 부품2.D10, PWM.1
  N8: 부품2.A5, X1.D+
  N9: 부품2.A4, X1.D-
  N10: Q2.Gate, R3.Pin_1, R4.Pin_0
  N11: Q2.drain, Fan.1, C1.1
