# Fritzing sketch main (saved by Fritzing 0.9.3b)
circuit board: 9.5cm x 9.5cm
breadboards: 1

parts:
  RTC = Real Time Clock Module - DS1307 RTC Breakout Board [part_number=RTC]
  POWER = Power Jack [package=power_jack_slot]
  Converter = LM2596-Step-Down-Converter [package=THT]
  ENCODER1 = Rotary Encoder with Knob
  Display = Grove OLED 128x96
  LIGHT = USB Connectors [package=usb-a-s]
  PWR_CTR = USB Connectors [package=usb-a-s]
  PUMP = Header 2 [part_number=PUMP package=molex-1x2_lock]
  LED_PWR = Header 2 [package=molex-1x2_lock]
  TEMP = Header 3 [package=molex-1x3_lock]
  Q1 = TRANSISTOR_NPN [package=to-92]
  R2 = Resistor [tolerance=±5% resistance=220 package=THT]
  C1 = Capacitor [package=cap-pth-small2]
  PH_probe = Header 4 [package=molex-1x4_lock]
  WATER_LEVEL = Header 3 [package=molex-1x3_lock]
  부품1 = Adafruit BME280 [part_number=BME280]
  NodeMCU = NodeMCU V3.0

nets:
  VIN: RTC.5V, Converter.pin3, Display.VCC, LIGHT.VBUS, PWR_CTR.VBUS, PUMP.2, TEMP.3, C1.2, PH_probe.4, WATER_LEVEL.3, 부품1.VIN, NodeMCU.Vin
  GND: RTC.GND, Converter.pin4, ENCODER1.no_name_yet#2, ENCODER1.no_name_yet#5, Display.GND, LIGHT.GND, PWR_CTR.GND, TEMP.1, Q1.E, PH_probe.2, PH_probe.3, WATER_LEVEL.1, 부품1.GND, NodeMCU.GND#6, NodeMCU.GND#13, NodeMCU.GND#16, NodeMCU.GND#33
  N1: RTC.SCL, Display.SCL, LIGHT.D+, PWR_CTR.D+, 부품1.SCK/SCL, NodeMCU.D5
  N2: RTC.SDA, Display.SDA, LIGHT.D-, PWR_CTR.D-, 부품1.SDI/SDA, NodeMCU.D3
  N3: POWER.GND, Converter.pin2, LED_PWR.1
  N4: POWER.PWR, Converter.pin1, LED_PWR.2
  N5: ENCODER1.no_name_yet#1, NodeMCU.D1
  N6: ENCODER1.no_name_yet#3, NodeMCU.D2
  N7: ENCODER1.no_name_yet#4, NodeMCU.D0
  N8: PUMP.1, Q1.C, C1.1
  N9: TEMP.2, NodeMCU.D6
  N10: Q1.B, R2.Pin_1
  N11: R2.Pin_0, NodeMCU.D8
  N12: PH_probe.1, NodeMCU.A0
  N13: WATER_LEVEL.2, NodeMCU.D7

notes:
  SDA
  SCL
  Vout
  Gout

custom parts:
  LM2596-Step-Down-Converter: A dummy, proxy, ersatz, stand-in part for whatever you want. With 4 pins on a 100 mil inline pin header footprint.
  Rotary Encoder with Knob: Rotary Encoder with 1/4" Shaft and Knob
  Adafruit BME280: Bosch has stepped up their game with their new BME280 sensor, an environmental sensor with temperature, barometric pressure and humidity! This sensor is great for all sorts of weather/environmental sensing and can even be used in both I2C and SPI! This precision sensor from Bosch is the best low-cost sensing solution for measuring humidity with ±3% accuracy, barometric pressure with ±1 hPa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
  NodeMCU V3.0: ESP8266 based NodeMCU
